// Logisim project Adas.circ as structural Verilog: 5 circuits, main circuit main
module main (
  input  Enable,
  input  Reset,
  output c1,
  output c0,
  output not_found,
  output found
);

  wire and_1_out, and_3_out, and_4_out, Clock_out, d_ff_1_q, expected_output_1_out_5, nor_1_out, or_1_out,
       validate_1_out_3, xor_1_out, xor_2_out;
  wire [1:0] Main_Counter_q;

  Clock Clock (.out(Clock_out));
  and and_1 (and_1_out, Clock_out, xor_1_out);
  xor xor_1 (xor_1_out, 1'b0, Enable);
  Counter #(.width(4), .max('hf)) Main_Counter (
    .Q({c1, c0, Main_Counter_q}), .clk(and_1_out), .clr(Reset));  // open: load, D, count, carry
  expected_output expected_output_1 (
    .Test_Case_0(Main_Counter_q[0]), .Test_Case_1(Main_Counter_q[1]), .IC_Type_1(c1), .IC_Type_0(c0),
    .out_5(expected_output_1_out_5));
  nor nor_1 (nor_1_out, Main_Counter_q[0], Main_Counter_q[1]);
  and and_2 (found, d_ff_1_q, or_1_out, nor_1_out);
  or or_1 (or_1_out, c1, c0);
  and and_3 (and_3_out, Main_Counter_q[0], Main_Counter_q[1]);
  not not_1 (not_found, found);
  xor xor_2 (xor_2_out, Main_Counter_q[0], Main_Counter_q[1]);
  Validate validate_1 (.in_1(xor_2_out), .in_2(expected_output_1_out_5), .out_3(validate_1_out_3));
  and and_4 (and_4_out, d_ff_1_q, validate_1_out_3);
  D_Flip_Flop #(.trigger("falling")) d_ff_1 (
    .clk(and_1_out), .D(and_4_out), .Q(d_ff_1_q), .preset(and_3_out), .en(1'b1));  // open: Qn, reset
  // AND_Gate and_5 is placed but not wired
  // OR_Gate or_2 is placed but not wired
  // XOR_Gate xor_3 is placed but not wired
  // NAND_Gate nand_1 is placed but not wired

  // Notes on the sheet:
  //   Expected Output
  //   Test IC
  //   validate
endmodule

module expected_output (
  input  Test_Case_0,
  input  Test_Case_1,
  input  IC_Type_1,
  input  IC_Type_0,
  output out_5
);

  wire and_1_out, nand_1_out, or_1_out, xor_1_out;

  or or_1 (or_1_out, Test_Case_0, Test_Case_1);
  xor xor_1 (xor_1_out, Test_Case_0, Test_Case_1);
  nand nand_1 (nand_1_out, Test_Case_0, Test_Case_1);
  and and_1 (and_1_out, Test_Case_0, Test_Case_1);
  Multiplexer #(.select(2)) multiplexer_1 (
    .in0(and_1_out), .in1(or_1_out), .in2(xor_1_out), .in3(nand_1_out), .out(out_5),
    .sel({IC_Type_1, IC_Type_0}));  // open: en
endmodule

module Validate (
  input  in_1,
  input  in_2,
  output out_3
);

  xnor xnor_1 (out_3, in_1, in_2);
endmodule

module Success (
  input  Enable,
  input  validate,
  input  reset,
  output Q
);

  wire and_1_out;

  and and_1 (and_1_out, Q, validate);
  D_Flip_Flop d_ff_1 (.clk(Enable), .D(and_1_out), .Q(Q), .preset(reset), .en(1'b1));  // open: Qn, reset
endmodule

module _2_4_MUX (
  input  C0,
  input  C1,
  input  I0,
  input  I1,
  input  I2,
  input  I3,
  output O
);

  wire and_1_out, and_2_out, and_3_out, and_4_out, not_1_out, not_2_out, not_3_out, not_4_out;

  not not_1 (not_1_out, C0);
  not not_2 (not_2_out, C1);
  not not_3 (not_3_out, C0);
  not not_4 (not_4_out, C1);
  and and_1 (and_1_out, not_1_out, not_2_out, I0);
  and and_2 (and_2_out, not_3_out, C1, I1);
  and and_3 (and_3_out, C0, not_4_out, I2);
  and and_4 (and_4_out, C0, C1, I3);
  or or_1 (O, and_1_out, and_2_out, and_3_out, and_4_out);
endmodule
