// Logisim project Ammar --Final.circ as structural Verilog: 9 circuits, main circuit main
module main (
  input  Enable,
  output c1,
  output c0,
  output Not_Found,
  output found
);

  wire and_3_out, Clock_out, get_validate_1_cd, get_validate_1_v, load_1_l, n74ls161_4_bit_counter_1_qa,
       n74ls161_4_bit_counter_1_qb, not_1_out, not_2_out, not_3_out, not_4_out, not_5_out, or_1_out,
       or_2_out, or_3_out, R_out;

  not not_1 (not_1_out, or_1_out);
  or or_1 (or_1_out, not_2_out, or_3_out);
  not not_2 (not_2_out, Enable);
  Clock Clock (.out(Clock_out));
  _74LS161_4_bit_counter u_74ls161_4_bit_counter_1 (
    .A(1'b0), .B(1'b0), .C(not_4_out), .D(or_2_out), .ENP(1'b1), .ENT(not_1_out), .CLK(Clock_out),
    .nCLR(not_3_out), .nLOAD(load_1_l), .QA(n74ls161_4_bit_counter_1_qa), .QB(n74ls161_4_bit_counter_1_qb),
    .QC(c0), .QD(c1));  // open: RCO
  not not_3 (not_3_out, R_out);
  Button R (.out(R_out));
  not not_4 (not_4_out, c0);
  or or_2 (or_2_out, c0, c1);
  Load load_1 (.nE(not_2_out), .V(get_validate_1_v), .AB(and_3_out), .L(load_1_l));
  or or_3 (or_3_out, Not_Found, found);
  Get_Validate get_validate_1 (
    .QA(n74ls161_4_bit_counter_1_qb), .QB(n74ls161_4_bit_counter_1_qa), .V(get_validate_1_v),
    .CD(get_validate_1_cd), .C___IC_type1(c0), .D___IC_type0(c1));
  not not_5 (not_5_out, get_validate_1_v);
  and and_1 (Not_Found, not_5_out, and_3_out);
  and and_2 (found, get_validate_1_v, get_validate_1_cd);
  and and_3 (and_3_out, c1, c0);
endmodule

module Get_Validate (
  input  QA,
  input  QB,
  input  C___IC_type1,
  input  D___IC_type0,
  output V,
  output CD
);

  wire expected_output_1_out_5, n4output_test_ic_1_ic0, n4output_test_ic_1_ic1, n4output_test_ic_1_ic2,
       n4output_test_ic_1_ic3, or_1_out;

  and and_1 (CD, QA, QB);
  or or_1 (or_1_out, QB, QA);
  expected_output expected_output_1 (
    .TC0_TC1(CD), .TC0___TC1(or_1_out), .IC_Type_1(C___IC_type1), .IC_Type_0(D___IC_type0),
    .out_5(expected_output_1_out_5));
  _4output_Test_IC u_4output_test_ic_1 (
    .A(QA), .B(QB), .IC0(n4output_test_ic_1_ic0), .IC1(n4output_test_ic_1_ic1), .IC2(n4output_test_ic_1_ic2),
    .IC3(n4output_test_ic_1_ic3));
  _4_Input_Validate u_4_input_validate_1 (
    .e(expected_output_1_out_5), .IC0(n4output_test_ic_1_ic0), .IC1(n4output_test_ic_1_ic1),
    .IC2(n4output_test_ic_1_ic2), .IC3(n4output_test_ic_1_ic3), .V(V));
  _4_Input_Validate u_4_input_validate_2 ();  // open: e, IC0, IC1, IC2, IC3, V
endmodule

module _4_Input_Validate (
  input  e,
  input  IC0,
  input  IC1,
  input  IC2,
  input  IC3,
  output V
);

  wire and_1_out, and_2_out, xnor_1_out, xnor_2_out, xnor_3_out, xnor_4_out;

  xnor xnor_1 (xnor_1_out, e, IC0);
  xnor xnor_2 (xnor_2_out, e, IC1);
  xnor xnor_3 (xnor_3_out, e, IC2);
  xnor xnor_4 (xnor_4_out, e, IC3);
  and and_1 (and_1_out, xnor_1_out, xnor_2_out);
  and and_2 (and_2_out, xnor_3_out, xnor_4_out);
  and and_3 (V, and_1_out, and_2_out);
endmodule

module expected_output (
  input  TC0_TC1,
  input  TC0___TC1,
  input  IC_Type_1,
  input  IC_Type_0,
  output out_5
);

  wire and_1_out, not_1_out;

  not not_1 (not_1_out, TC0_TC1);
  and and_1 (and_1_out, TC0___TC1, not_1_out);
  Multiplexer #(.select(2)) multiplexer_1 (
    .in0(TC0_TC1), .in1(TC0___TC1), .in2(and_1_out), .in3(not_1_out), .out(out_5),
    .sel({IC_Type_0, IC_Type_1}));  // open: en
endmodule

module Load (
  input  nE,
  input  V,
  input  AB,
  output L
);

  wire or_1_out;

  or or_1 (or_1_out, nE, AB);
  or or_2 (L, or_1_out, V);
endmodule

module _4output_Test_IC (
  input  A,
  input  B,
  output IC0,
  output IC1,
  output IC2,
  output IC3
);

  or or_1 (IC0, A, B);
  or or_2 (IC1, A, B);
  or or_3 (IC2, A, B);
  or or_4 (IC3, A, B);
  // XNOR_Gate xnor_1 is placed but not wired
  // XNOR_Gate xnor_2 is placed but not wired
  // XNOR_Gate xnor_3 is placed but not wired
  // XNOR_Gate xnor_4 is placed but not wired
  // NOR_Gate nor_1 is placed but not wired
  // NOR_Gate nor_2 is placed but not wired
  // NOR_Gate nor_3 is placed but not wired
  // NOR_Gate nor_4 is placed but not wired
  // XOR_Gate xor_1 is placed but not wired
  // XOR_Gate xor_2 is placed but not wired
  // XOR_Gate xor_3 is placed but not wired
  // XOR_Gate xor_4 is placed but not wired
  // AND_Gate and_1 is placed but not wired
  // NAND_Gate nand_1 is placed but not wired
  // NAND_Gate nand_2 is placed but not wired
  // AND_Gate and_2 is placed but not wired
  // NAND_Gate nand_3 is placed but not wired
  // AND_Gate and_3 is placed but not wired
  // NAND_Gate nand_4 is placed but not wired
  // AND_Gate and_4 is placed but not wired
endmodule

module _74LS161_4_bit_counter (
  input  A,
  input  B,
  input  C,
  input  D,
  input  CLK,
  input  ENP,
  input  ENT,
  input  nLOAD,
  input  nCLR,
  output QA,
  output QB,
  output QC,
  output QD,
  output RCO
);

  wire and_1_out, and_2_out, not_1_out, not_2_out;

  and and_1 (and_1_out, ENP, ENT);
  and and_2 (and_2_out, and_1_out, nLOAD);
  not not_1 (not_1_out, nLOAD);
  Counter #(.width(4), .max('hf)) counter_1 (
    .load(not_1_out), .D({D, C, B, A}), .count(and_2_out), .Q({QD, QC, QB, QA}), .carry(RCO), .clk(CLK),
    .clr(not_2_out));
  not not_2 (not_2_out, nCLR);
endmodule

module Test (
  input  G0,
  input  G1,
  input  G2,
  input  G3,
  input  e,
  output V
);

  wire and_1_out, and_2_out, and_3_out, and_4_out, and_5_out, and_6_out, and_7_out, and_8_out, not_1_out,
       not_2_out, not_3_out, not_4_out, not_5_out;

  not not_1 (not_1_out, G0);
  not not_2 (not_2_out, G1);
  and and_1 (and_1_out, not_1_out, not_2_out);
  not not_3 (not_3_out, G2);
  not not_4 (not_4_out, G3);
  not not_5 (not_5_out, e);
  and and_2 (and_2_out, G0, G1);
  and and_3 (and_3_out, and_1_out, not_3_out);
  and and_4 (and_4_out, and_3_out, and_5_out);
  and and_5 (and_5_out, not_4_out, not_5_out);
  and and_6 (and_6_out, and_2_out, G2);
  and and_7 (and_7_out, and_6_out, and_8_out);
  and and_8 (and_8_out, G3, e);
  or or_1 (V, and_4_out, and_7_out);
endmodule

module Test_2 (
  input  e,
  input  IC0,
  input  IC1,
  input  IC2,
  input  IC3,
  output V
);

  wire and_1_out, xnor_1_out, xnor_2_out, xnor_3_out;

  xnor xnor_1 (xnor_1_out, IC0, IC1);
  xnor xnor_2 (xnor_2_out, IC2, IC3);
  and and_1 (and_1_out, xnor_1_out, xnor_2_out);
  and and_2 (V, and_1_out, xnor_3_out);
  xnor xnor_3 (xnor_3_out, IC0, e);
endmodule
