# Fritzing sketch Sketch (saved by Fritzing 0.9.3b)
breadboards: 4

parts:
  counter = 74HC595 [package="DIP16 [THT]"]
  VCC1 = Battery
  LED1 = LED - 5mm [color="Red (633nm)" package="5 mm [THT]"]
  LED2 = LED - 5mm [color="Red (633nm)" package="5 mm [THT]"]
  LED3 = LED - 5mm [color="Red (633nm)" package="5 mm [THT]"]
  LED4 = LED - 5mm [color="Red (633nm)" package="5 mm [THT]"]
  LED5 = LED - 5mm [color="Red (633nm)" package="5 mm [THT]"]
  LED6 = LED - 5mm [color="Red (633nm)" package="5 mm [THT]"]
  S1 = Pushbutton [package="[THT]"]
  S2 = Pushbutton [package="[THT]"]  # not connected
  S3 = Pushbutton [package="[THT]"]
  XOR = 74HC595 [package="DIP16 [THT]"]

nets:
  N1: counter.Q1, S3.Pin_1, S3.Pin_2, S3.Pin_3, S3.Pin_4
  N2: counter.Q2, S1.Pin_1, S1.Pin_2, S1.Pin_3, S1.Pin_4
  N3: counter.Q3, XOR.Q3
  GND: counter.Q5, counter.Q6, counter.GND, VCC1.-, LED1.cathode, LED2.cathode, LED3.cathode, LED4.cathode, LED5.cathode, LED6.cathode, XOR.GND
  N4: counter.OE, XOR.Q2
  N5: counter.DS, XOR.Q1
  VCC: counter.VCC, VCC1.+, XOR.VCC
